// Logisim project minicomputer.circ as structural Verilog: 4 circuits, main circuit main
module main (
  input  [7:0] in_1
);

  Clock clock_1 ();  // open: out
  datapath datapath_1 ();  // open: clk, reset
  ALU alu_1 ();  // open: D1, D2, control, carry_in, R, carry_out, borrow_out, mult_carry_out, remain, major, equal, minor

  // Notes on the sheet:
  //   big_endian
endmodule

module datapath (
  input  clk,
  input  reset
);

  wire [2:0] alucode, rd, rs, rt;
  wire [3:0] opcode;
  wire [15:0] alu_1_r, c_inst, n_inst, PC_q, registers_database_1_r1, registers_database_1_r2;

  Register #(.width(16)) PC (.D(n_inst), .clk(clk), .Q(PC_q), .clr(reset));  // open: en
  Register #(.width(16)) IR (.D(c_inst), .clk(clk), .Q({alucode, rt, rs, rd, opcode}), .clr(reset));  // open: en
  Register #(.width(16)) MAR (.clk(clk), .clr(reset));  // open: D, en, Q
  Register #(.width(16)) MDR (.clk(clk), .clr(reset));  // open: D, en, Q
  RAM #(.addrWidth(16), .dataWidth(16)) instruction_memory (
    .addr(PC_q), .clk(clk), .dout(c_inst));  // open: we, oe, din
  registers_database registers_database_1 (
    .read_reg1(rs), .read_reg2(rt), .write_reg(rd), .clk(clk), .R1(registers_database_1_r1),
    .R2(registers_database_1_r2));  // open: DATA, reg_write
  ALU alu_1 (
    .D1(registers_database_1_r1), .D2(registers_database_1_r2), .control(alucode), .R(alu_1_r));  // open: carry_in, carry_out, borrow_out, mult_carry_out, remain, major, equal, minor
  RAM #(.addrWidth(16), .dataWidth(16)) data_memory (
    .addr(alu_1_r), .clk(clk), .din(registers_database_1_r2));  // open: we, oe, dout
endmodule

module registers_database (
  input  [15:0] DATA,
  input  reg_write,
  input  [2:0] read_reg1,
  input  [2:0] read_reg2,
  input  [2:0] write_reg,
  input  clk,
  output [15:0] R1,
  output [15:0] R2
);

  wire decoder_1_out0, decoder_1_out1, decoder_1_out2, decoder_1_out3, decoder_1_out4, decoder_1_out5,
       decoder_1_out6, decoder_1_out7;
  wire [15:0] register_1_q, register_2_q, register_3_q, register_4_q, register_5_q, register_6_q,
       register_7_q, register_8_q;

  Decoder #(.select(3)) decoder_1 (
    .out0(decoder_1_out0), .out1(decoder_1_out1), .out2(decoder_1_out2), .out3(decoder_1_out3),
    .out4(decoder_1_out4), .out5(decoder_1_out5), .out6(decoder_1_out6), .out7(decoder_1_out7),
    .sel(write_reg), .en(reg_write));
  Register #(.width(16)) register_1 (.D(DATA), .en(decoder_1_out0), .clk(clk), .Q(register_1_q));  // open: clr
  Register #(.width(16)) register_2 (.D(DATA), .en(decoder_1_out4), .clk(clk), .Q(register_2_q));  // open: clr
  Register #(.width(16)) register_3 (.D(DATA), .en(decoder_1_out1), .clk(clk), .Q(register_3_q));  // open: clr
  Register #(.width(16)) register_4 (.D(DATA), .en(decoder_1_out5), .clk(clk), .Q(register_4_q));  // open: clr
  Register #(.width(16)) register_5 (.D(DATA), .en(decoder_1_out2), .clk(clk), .Q(register_5_q));  // open: clr
  Register #(.width(16)) register_6 (.D(DATA), .en(decoder_1_out6), .clk(clk), .Q(register_6_q));  // open: clr
  Register #(.width(16)) register_7 (.D(DATA), .en(decoder_1_out3), .clk(clk), .Q(register_7_q));  // open: clr
  Register #(.width(16)) register_8 (.D(DATA), .en(decoder_1_out7), .clk(clk), .Q(register_8_q));  // open: clr
  Multiplexer #(.select(3), .width(16)) multiplexer_1 (
    .in0(register_1_q), .in1(register_3_q), .in2(register_5_q), .in3(register_7_q), .in4(register_2_q),
    .in5(register_4_q), .in6(register_6_q), .in7(register_8_q), .out(R1), .sel(read_reg1));
  Multiplexer #(.select(3), .width(16)) multiplexer_2 (
    .in0(register_1_q), .in1(register_3_q), .in2(register_5_q), .in3(register_7_q), .in4(register_2_q),
    .in5(register_4_q), .in6(register_6_q), .in7(register_8_q), .out(R2), .sel(read_reg2));
endmodule

module ALU (
  input  [15:0] D1,
  input  [15:0] D2,
  input  [2:0] control,
  input  [15:0] carry_in,
  output [15:0] R,
  output carry_out,
  output borrow_out,
  output [15:0] mult_carry_out,
  output [15:0] remain,
  output major,
  output equal,
  output minor
);

  wire [15:0] adder_1_out, and_1_out, divider_1_out, multiplier_1_out, or_1_out, shifter_1_out,
       shifter_2_out, subtractor_1_out;

  Comparator #(.width(16)) comparator_1 (.a(D1), .b(D2), .gt(major), .eq(equal), .lt(minor));
  Adder #(.width(16)) adder_1 (.a(D1), .b(D2), .out(adder_1_out), .cin(carry_in[0]), .cout(carry_out));
  Subtractor #(.width(16)) subtractor_1 (.a(D1), .b(D2), .out(subtractor_1_out), .bin(carry_in[0]), .bout(borrow_out));
  Multiplier #(.width(16)) multiplier_1 (.a(D1), .b(D2), .out(multiplier_1_out), .cin(carry_in), .cout(mult_carry_out));
  Divider #(.width(16)) divider_1 (.a(D1), .b(D2), .out(divider_1_out), .upper(carry_in), .rem(remain));
  Shifter #(.shift("lr"), .width(16)) shifter_1 (.out(shifter_1_out));  // open: in, dist
  Shifter #(.width(16)) shifter_2 (.in(D1), .\dist (D2[3:0]), .out(shifter_2_out));
  assign and_1_out = D2 & D1;  // AND_Gate and_1, 16 bits wide
  assign or_1_out = D2 | D1;  // OR_Gate or_1, 16 bits wide
  Multiplexer #(.select(3), .width(16)) multiplexer_1 (
    .in0(adder_1_out), .in1(subtractor_1_out), .in2(multiplier_1_out), .in3(divider_1_out), .in4(and_1_out),
    .in5(or_1_out), .in6(shifter_1_out), .in7(shifter_2_out), .out(R), .sel(control));

  // Notes on the sheet:
  //   sub
  //   mult
  //   div
  //   add
  //   or
  //   and
  //   shft_r
  //   shift_l
endmodule
